# Fritzing sketch controller (saved by Fritzing 0.9.4)
circuit board: 9.63682cm x 5.79071cm
breadboards: 1

parts:
  U1 = ATTiny84 [package=dip]
  V1 = DC Power [voltage=5]
  C1 = Capacitor Polarized [package=nippon_f80]
  R1 = Resistor [tolerance=±5% resistance=100 package="2512 [SMD]"]
  R2 = Resistor [tolerance=±5% resistance=100 package="2512 [SMD]"]
  S1 = Round Pushbutton
  C2 = Capacitor Polarized [package=nippon_f80]
  R3 = Resistor [tolerance=±5% resistance=100 package="2512 [SMD]"]
  R4 = Resistor [tolerance=±5% resistance=100 package="2512 [SMD]"]
  S2 = Round Pushbutton
  J1 = Camdenboss CTB0158-2 [part_number=CTB0158-2 package=THT]
  IC1 = L293D [package=THT]  # not connected
  J2 = Camdenboss CTB0158-6 [part_number=CTB0158-6 package=THT]  # not connected

nets:
  N1: U1.pin1, V1.V-
  N2: U1.pin2, R1.Pin_1, R2.Pin_1
  N3: U1.pin3, R3.Pin_1, R4.Pin_1
  N4: U1.pin12, J1.pin2
  N5: U1.pin13, J1.pin1
  GND: U1.pin14, V1.V+, C1.-, S1.leg0, C2.-, S2.leg0
  N6: C1.+, R1.Pin_0
  N7: R2.Pin_0, S1.leg1
  N8: C2.+, R4.Pin_0
  N9: R3.Pin_0, S2.leg1

custom parts:
  ATTiny84: Atmel ATTiny84 processor. 8 ADC pins, 4 PWM pins. Available in either 10MHz or 20MHz. The last 2 pin numbers refer to arduino. D6 = Arduino 6, A6 = Arduino A6 example: PA6 (SDA/MOSI/OC1A/DI/AD6/PCINT6/D6/A6) NOTE: This part is diagrammed to suit the MIT HLT ATTiny84 core at https://github.com/damellis/attiny/
